// Logisim project 22BCM026_22BCM027_snakes and ladders.circ as structural Verilog: 1 circuit, main circuit main
module main (
);

  wire _7_2_out, _7_out, _18_2_out, _18_out, _31_2_out, _31_out, _47_2_out, _47_out, _48_2_out, _48_out,
       _52_2_out, _52_out, _65_2_out, _65_out, _66_2_out, _66_out, _77_2_out, _77_out, _78_2_out, _78_out,
       _83_2_out, _83_out, _98_2_out, _98_out, and_1_out, and_2_out, and_3_out, and_4_out, and_5_out,
       and_6_out, and_7_out, and_8_out, and_9_out, button_1_out, button_2_out, decoder_1_out0,
       decoder_1_out1, decoder_1_out2, decoder_1_out3, decoder_1_out4, decoder_1_out5, decoder_1_out6,
       decoder_1_out7, not_1_out, not_2_out, not_3_out, not_4_out, not_5_out, not_6_out, not_7_out,
       not_8_out, not_9_out, not_10_out, not_11_out, not_12_out, not_13_out, not_14_out, not_15_out,
       not_16_out, not_17_out, not_18_out, not_19_out, not_20_out, or_1_out, or_2_out, or_3_out, or_4_out,
       or_5_out, or_6_out, or_7_out, or_8_out, or_9_out, or_10_out, or_11_out, or_12_out, or_13_out,
       t_ff_1_q, undriven, undriven_2, undriven_3, undriven_4, undriven_5, undriven_6, undriven_7,
       undriven_8, undriven_9, undriven_10, undriven_11, undriven_12;
  wire [2:0] demultiplexer_1_out0, demultiplexer_1_out1, random_1_out;
  wire [6:0] adder_1_out, adder_2_out, adder_3_out, adder_4_out, demultiplexer_2_out0, demultiplexer_2_out1,
       demultiplexer_3_out0, demultiplexer_3_out1, multiplexer_1_out, multiplexer_2_out, multiplexer_3_out,
       multiplexer_4_out, multiplexer_5_out, register_1_q, register_2_q, subtractor_1_out, subtractor_2_out;

  Button button_1 (.out(button_1_out));
  Button button_2 (.out(button_2_out));
  Random #(.width(3)) random_1 (.clk(button_1_out), .next(button_1_out), .out(random_1_out), .clr(button_2_out));
  Demultiplexer #(.width(3), .enable("false")) demultiplexer_1 (
    .out0(demultiplexer_1_out0), .out1(demultiplexer_1_out1), .in(random_1_out), .sel(t_ff_1_q));
  not not_1 (not_1_out, adder_2_out[6]);
  Decoder #(.select(3), .enable("false")) decoder_1 (
    .out0(decoder_1_out0), .out1(decoder_1_out1), .out2(decoder_1_out2), .out3(decoder_1_out3),
    .out4(decoder_1_out4), .out5(decoder_1_out5), .out6(decoder_1_out6), .out7(decoder_1_out7),
    .sel(random_1_out));
  T_Flip_Flop t_ff_1 (.clk(button_1_out), .T(1'b1), .Q(t_ff_1_q), .reset(button_2_out));  // open: Qn, preset, en
  not not_2 (not_2_out, adder_1_out[6]);
  not not_3 (not_3_out, adder_2_out[5]);
  not not_4 (not_4_out, adder_2_out[4]);
  not not_5 (not_5_out, adder_1_out[5]);
  not not_6 (not_6_out, adder_1_out[4]);
  not not_7 (not_7_out, adder_2_out[2]);
  not not_8 (not_8_out, adder_2_out[3]);
  Register #(.width(7)) register_1 (
    .D(multiplexer_1_out), .en(1'b1), .Q(register_1_q), .clk(button_1_out), .clr(button_2_out));
  not not_9 (not_9_out, adder_1_out[2]);
  not not_10 (not_10_out, adder_1_out[3]);
  Register #(.width(7)) register_2 (
    .D(multiplexer_2_out), .en(1'b1), .Q(register_2_q), .clk(button_1_out), .clr(button_2_out));
  not not_11 (not_11_out, adder_2_out[1]);
  not not_12 (not_12_out, adder_2_out[0]);
  or or_1 (or_1_out, decoder_1_out6, decoder_1_out5, decoder_1_out3, decoder_1_out4, decoder_1_out2);
  not not_13 (not_13_out, adder_1_out[1]);
  not not_14 (not_14_out, adder_1_out[0]);
  or or_2 (or_2_out, decoder_1_out6, decoder_1_out5, decoder_1_out4, decoder_1_out0);
  _7_Segment_Display u_7_segment_display_1 (
    .g(or_1_out), .f(or_2_out), .a(or_5_out), .b(or_7_out), .e(or_4_out), .d(or_3_out), .c(or_6_out));  // open: dp
  or or_3 (or_3_out, decoder_1_out0, decoder_1_out2, decoder_1_out3, decoder_1_out5, decoder_1_out6);
  or or_4 (or_4_out, decoder_1_out0, decoder_1_out2, decoder_1_out6);
  Adder #(.width(7)) adder_1 (
    .a({4'b0000, demultiplexer_1_out1}), .b(register_1_q), .out(adder_1_out));  // open: cin, cout
  Multiplexer #(.width(7), .enable("false")) multiplexer_1 (
    .in0(multiplexer_3_out), .in1(subtractor_1_out), .out(multiplexer_1_out), .sel(or_11_out));
  Adder #(.width(7)) adder_2 (
    .a({4'b0000, demultiplexer_1_out0}), .b(register_2_q), .out(adder_2_out));  // open: cin, cout
  and _7 (_7_out, adder_2_out[0], adder_2_out[1], adder_2_out[2], not_8_out, not_4_out, not_3_out, not_1_out);
  and _18 (_18_out, not_12_out, adder_2_out[1], not_7_out, not_8_out, adder_2_out[4], not_3_out, not_1_out);
  and _47 (_47_out, adder_2_out[0], adder_2_out[1], adder_2_out[2], adder_2_out[3], not_4_out, adder_2_out[5], not_1_out);
  and _52 (_52_out, not_12_out, not_11_out, adder_2_out[2], not_8_out, adder_2_out[4], adder_2_out[5], not_1_out);
  and _77 (_77_out, adder_2_out[0], adder_2_out[1], adder_2_out[2], adder_2_out[3], not_4_out, not_3_out, adder_2_out[6]);
  and _66 (_66_out, not_12_out, adder_2_out[1], not_7_out, not_8_out, not_4_out, not_3_out, adder_2_out[6]);
  and _48 (_48_out, not_12_out, not_11_out, not_7_out, not_8_out, adder_2_out[4], adder_2_out[5], not_1_out);
  and _65 (_65_out, adder_2_out[0], not_11_out, not_7_out, not_8_out, not_4_out, not_3_out, adder_2_out[6]);
  and _78 (_78_out, not_12_out, adder_2_out[1], adder_2_out[2], adder_2_out[3], not_4_out, not_3_out, adder_2_out[6]);
  and _98 (_98_out, not_12_out, adder_2_out[1], not_7_out, not_8_out, not_4_out, adder_2_out[5], adder_2_out[6]);
  and _83 (_83_out, adder_2_out[0], adder_2_out[1], not_7_out, not_8_out, adder_2_out[4], not_3_out, adder_2_out[6]);
  and _31 (_31_out, adder_2_out[0], adder_2_out[1], adder_2_out[2], adder_2_out[3], adder_2_out[4], not_3_out, not_1_out);
  or or_5 (or_5_out, decoder_1_out6, decoder_1_out5, decoder_1_out7, decoder_1_out3, decoder_1_out2, decoder_1_out0);
  or or_6 (or_6_out, decoder_1_out6, decoder_1_out3, decoder_1_out5, decoder_1_out4, decoder_1_out0, decoder_1_out7, decoder_1_out1);
  // Probe on adder_1_out
  and _7_2 (_7_2_out, adder_1_out[0], adder_1_out[1], adder_1_out[2], not_10_out, not_6_out, not_5_out, not_2_out);
  and _18_2 (_18_2_out, not_14_out, adder_1_out[1], not_9_out, not_10_out, adder_1_out[4], not_5_out, not_2_out);
  and _47_2 (_47_2_out, adder_1_out[0], adder_1_out[1], adder_1_out[2], adder_1_out[3], not_6_out, adder_1_out[5], not_2_out);
  and _52_2 (_52_2_out, not_14_out, not_13_out, adder_1_out[2], not_10_out, adder_1_out[4], adder_1_out[5], not_2_out);
  and _77_2 (_77_2_out, adder_1_out[0], not_13_out, adder_1_out[2], adder_1_out[3], not_6_out, not_5_out, adder_1_out[6]);
  and _66_2 (_66_2_out, not_14_out, adder_1_out[1], not_9_out, not_10_out, not_6_out, not_5_out, adder_1_out[6]);
  and _48_2 (_48_2_out, not_14_out, not_13_out, not_9_out, not_10_out, adder_1_out[4], adder_1_out[5], not_2_out);
  and _65_2 (_65_2_out, adder_1_out[0], not_13_out, not_9_out, not_10_out, not_6_out, not_5_out, adder_1_out[6]);
  and _78_2 (_78_2_out, not_14_out, adder_1_out[1], adder_1_out[2], adder_1_out[3], not_6_out, not_5_out, adder_1_out[6]);
  and _98_2 (_98_2_out, not_14_out, adder_1_out[1], not_9_out, not_10_out, not_6_out, adder_1_out[5], adder_1_out[6]);
  and _83_2 (_83_2_out, adder_1_out[0], adder_1_out[1], not_9_out, not_10_out, adder_1_out[4], not_5_out, adder_1_out[6]);
  and _31_2 (_31_2_out, adder_1_out[0], adder_1_out[1], adder_1_out[2], adder_1_out[3], adder_1_out[4], not_5_out, not_2_out);
  Multiplexer #(.width(7), .enable("false")) multiplexer_2 (
    .in0(multiplexer_4_out), .in1(subtractor_2_out), .out(multiplexer_2_out), .sel(or_10_out));
  or or_7 (or_7_out, decoder_1_out4, decoder_1_out3, decoder_1_out7, decoder_1_out2, decoder_1_out1, decoder_1_out0);
  Demultiplexer #(.width(7), .enable("false")) demultiplexer_2 (
    .out0(demultiplexer_2_out0), .out1(demultiplexer_2_out1), .in(adder_1_out), .sel(or_9_out));
  Multiplexer #(.width(7), .enable("false")) multiplexer_3 (
    .in0(demultiplexer_2_out0), .in1(adder_3_out), .out(multiplexer_3_out), .sel(or_9_out));
  // Probe on adder_2_out
  or or_8 (or_8_out, _7_out, _18_out, _47_out, _52_out, _77_out, _66_out);
  // Probe on multiplexer_2_out
  // Probe on multiplexer_1_out
  or or_9 (or_9_out, _7_2_out, _18_2_out, _47_2_out, _52_2_out, _77_2_out, _66_2_out);
  Demultiplexer #(.width(7), .enable("false")) demultiplexer_3 (
    .out0(demultiplexer_3_out0), .out1(demultiplexer_3_out1), .in(adder_2_out), .sel(or_8_out));
  Multiplexer #(.width(7), .enable("false")) multiplexer_4 (
    .in0(demultiplexer_3_out0), .in1(adder_4_out), .out(multiplexer_4_out), .sel(or_8_out));
  LED led_1 ();  // open: in
  LED _100 ();  // open: in
  LED _99 ();  // open: in
  LED _98_3 (.in(undriven_2));
  LED _81 ();  // open: in
  LED _82 ();  // open: in
  LED _83_3 (.in(undriven_3));
  LED _79 ();  // open: in
  LED _80 ();  // open: in
  LED _78_3 (.in(undriven_4));
  LED _62 ();  // open: in
  LED _61 ();  // open: in
  LED _63 ();  // open: in
  LED _60 ();  // open: in
  LED _58 (.in(undriven_3));
  LED _59 ();  // open: in
  LED _42 ();  // open: in
  LED _43 ();  // open: in
  LED _41 ();  // open: in
  LED _40 (.in(undriven_7));
  LED _39 ();  // open: in
  LED _38 (.in(undriven));
  LED _23 (.in(undriven_5));
  LED _21 ();  // open: in
  LED _22 ();  // open: in
  LED _19 ();  // open: in
  LED _18_3 (.in(undriven));
  LED _20 ();  // open: in
  LED _2 ();  // open: in
  LED _1 ();  // open: in
  LED _3 ();  // open: in
  or or_10 (or_10_out, _48_out, _65_out, _78_out, _98_out, _83_out, _31_out);
  LED _96 ();  // open: in
  LED _97 (.in(undriven_6));
  LED _85 ();  // open: in
  LED _84 ();  // open: in
  LED _77_3 (.in(undriven_6));
  LED _76 ();  // open: in
  LED _64 ();  // open: in
  LED _65_3 (.in(undriven_7));
  LED _56 ();  // open: in
  LED _57 ();  // open: in
  LED _45 ();  // open: in
  LED _44 ();  // open: in
  LED _36 ();  // open: in
  LED _37 ();  // open: in
  LED _25 ();  // open: in
  LED _24 ();  // open: in
  LED _16 ();  // open: in
  LED _17 ();  // open: in
  LED _5 ();  // open: in
  LED _4 ();  // open: in
  or or_11 (or_11_out, _48_2_out, _65_2_out, _78_2_out, _98_2_out, _83_2_out, _31_2_out);
  LED _94 ();  // open: in
  LED _93 ();  // open: in
  LED _95 ();  // open: in
  LED _88 ();  // open: in
  LED _87 ();  // open: in
  LED _86 (.in(undriven_8));
  LED _75 ();  // open: in
  LED _73 (.in(undriven_2));
  LED _74 ();  // open: in
  LED _66_3 (.in(undriven_8));
  LED _68 ();  // open: in
  LED _67 (.in(undriven_9));
  LED _53 (.in(undriven_4));
  LED _55 ();  // open: in
  LED _54 ();  // open: in
  LED _47_3 (.in(undriven_9));
  LED _46 ();  // open: in
  LED _48_3 (.in(undriven_5));
  LED _33 ();  // open: in
  LED _35 ();  // open: in
  LED _34 ();  // open: in
  LED _26 ();  // open: in
  LED _28 ();  // open: in
  LED _27 (.in(undriven_10));
  LED _14 ();  // open: in
  LED _15 ();  // open: in
  LED _13 ();  // open: in
  LED _7_3 (.in(undriven_10));
  LED _8 ();  // open: in
  LED _6 (.in(undriven_12));
  // Probe on adder_3_out
  Adder #(.width(7)) adder_3 (.a(7'b0010100), .b(demultiplexer_2_out1), .out(adder_3_out));  // open: cin, cout
  Subtractor #(.width(7)) subtractor_1 (.a(adder_1_out), .b(7'b0011001), .out(subtractor_1_out));  // open: bin, bout
  // Probe on subtractor_1_out
  Adder #(.width(7)) adder_4 (.a(7'b0010100), .b(demultiplexer_3_out1), .out(adder_4_out));  // open: cin, cout
  LED led_2 ();  // open: in
  LED _91 ();  // open: in
  LED _92 ();  // open: in
  LED _89 ();  // open: in
  LED _90 ();  // open: in
  LED _71 ();  // open: in
  LED _72 (.in(undriven_11));
  LED _70 ();  // open: in
  LED _69 ();  // open: in
  LED _51 ();  // open: in
  LED _52_3 (.in(undriven_11));
  LED _49 ();  // open: in
  LED _50 ();  // open: in
  LED _32 ();  // open: in
  LED _31_3 (.in(undriven_12));
  LED _29 ();  // open: in
  LED _30 ();  // open: in
  LED _12 ();  // open: in
  LED _11 ();  // open: in
  LED _10 ();  // open: in
  LED _9 ();  // open: in
  Multiplexer #(.width(7), .enable("false")) multiplexer_5 (
    .in0(multiplexer_2_out), .in1(multiplexer_1_out), .out(multiplexer_5_out), .sel(t_ff_1_q));
  // Probe on subtractor_2_out
  Subtractor #(.width(7)) subtractor_2 (.a(adder_2_out), .b(7'b0011001), .out(subtractor_2_out));  // open: bin, bout
  not not_15 (not_15_out, multiplexer_5_out[0]);
  not not_16 (not_16_out, multiplexer_5_out[1]);
  // Probe on adder_4_out
  _7_Segment_Display u_7_segment_display_2 (
    .g(and_1_out), .a(and_1_out), .b(or_12_out), .e(and_1_out), .d(and_1_out), .c(and_2_out));  // open: f, dp
  and and_1 (and_1_out, or_13_out, not_17_out);
  not not_17 (not_17_out, t_ff_1_q);
  not not_18 (not_18_out, multiplexer_5_out[2]);
  not not_19 (not_19_out, multiplexer_5_out[3]);
  not not_20 (not_20_out, multiplexer_5_out[4]);
  or or_12 (or_12_out, and_1_out, and_2_out);
  and and_2 (and_2_out, t_ff_1_q, or_13_out);
  and and_3 (and_3_out, not_15_out, multiplexer_5_out[1], not_18_out, multiplexer_5_out[3], not_20_out, multiplexer_5_out[5], multiplexer_5_out[6]);
  and and_4 (and_4_out, multiplexer_5_out[0], not_16_out, not_18_out, multiplexer_5_out[3], not_20_out, multiplexer_5_out[5], multiplexer_5_out[6]);
  and and_5 (and_5_out, not_15_out, not_16_out, not_18_out, multiplexer_5_out[3], not_20_out, multiplexer_5_out[5], multiplexer_5_out[6]);
  and and_6 (and_6_out, multiplexer_5_out[0], multiplexer_5_out[1], multiplexer_5_out[2], not_19_out, not_20_out, multiplexer_5_out[5], multiplexer_5_out[6]);
  and and_7 (and_7_out, not_15_out, multiplexer_5_out[1], multiplexer_5_out[2], not_19_out, not_20_out, multiplexer_5_out[5], multiplexer_5_out[6]);
  and and_8 (and_8_out, multiplexer_5_out[0], not_16_out, multiplexer_5_out[2], not_19_out, not_20_out, multiplexer_5_out[5], multiplexer_5_out[6]);
  and and_9 (and_9_out, not_15_out, not_16_out, multiplexer_5_out[2], not_19_out, not_20_out, multiplexer_5_out[5], multiplexer_5_out[6]);
  or or_13 (or_13_out, and_3_out, and_4_out, and_5_out, and_6_out, and_7_out, and_8_out, and_9_out);

  // Notes on the sheet:
  //   DICE
  //   CLEAR
  //   BOARD
  //   Ladders
  //   Ladders
  //   Snakes
  //   Snakes
  //   SNAKES AND LADDERS
  //   Snakes
  //   Ladders
  //   P-      Wins
endmodule
